// Digital circuit full_adder.dig as structural Verilog
module full_adder (
  input  A,
  input  B,
  input  C_2,
  output c,
  output c_out
);

  wire and_1_out, and_2_out, xor_1_out;

  xor xor_1 (xor_1_out, A, B);
  xor xor_2 (c, xor_1_out, C_2);
  and and_1 (and_1_out, C_2, xor_1_out);
  and and_2 (and_2_out, A, B);
  or or_1 (c_out, and_1_out, and_2_out);

  // Notes on the sheet:
  //   * taken from professor's answer
endmodule
